# Fritzing sketch fermentpressure (saved by Fritzing 1.0.7)
stripboards: 1

parts:
  OLED_I2C1 = OLED 128x64 I2C Monochrome Display
  Pressure_Connect = female pin header, 4 pins [form="♀ (female)"]
  Solenoid_Control = IFR520 MOS module [package=THT]
  R1 = Resistor [tolerance=±5% power=0.25W resistance=1k package=THT]
  Temp_connect = female pin header, 4 pins [form="♀ (female)"]
  i2c_-_Display = female pin header, 4 pins [form="♀ (female)"]
  R2 = Resistor [tolerance=±5% power=0.25W resistance=2.2k package=THT]
  M1 = DOIT Esp32 DevKit v1 (30 pins long, 11 pins width) [part_number=ESP32S-PIN30]
  R3 = Resistor [tolerance=±5% power=0.25W resistance=4.7k package=THT]

nets:
  N1: OLED_I2C1.SDA, i2c_-_Display.pin4, M1.D21
  N2: OLED_I2C1.SCK, i2c_-_Display.pin3, M1.D22
  VDD: OLED_I2C1.VDD, Solenoid_Control.VCC, Temp_connect.pin2, i2c_-_Display.pin2, M1.3V3, R3.Pin_1
  GND: OLED_I2C1.GND, Pressure_Connect.pin1, Solenoid_Control.GND, Temp_connect.pin1, i2c_-_Display.pin1, R2.Pin_1, M1.GND
  N3: Pressure_Connect.pin2, M1.VIN
  N4: Pressure_Connect.pin3, R1.Pin_1
  N5: Solenoid_Control.SIG, M1.D27
  N6: R1.Pin_0, R2.Pin_0, M1.D34
  N7: Temp_connect.pin3, M1.D4, R3.Pin_0

custom parts:
  DOIT Esp32 DevKit v1 (30 pins long, 11 pins width): The DOIT Esp32 DevKit v1 is one of the development board created by DOIT to evaluate the ESP-WROOM-32 module. It is based on the ESP32 microcontroller that boasts Wifi, Bluetooth, Ethernet and Low Power support all in a single chip. (vanepp) made breadboard work, adjusted pin numbering and labels and reduced size of schematic and cleaned up pcb. This chip is 30pins long (2 x15) and 11 pins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
