# Fritzing sketch fermentpressure_v2 (saved by Fritzing 1.0.7)
stripboards: 1

parts:
  OLED_I2C1 = OLED 128x64 I2C Monochrome Display  # not connected
  R1 = Resistor [tolerance=±5% power=0.25W resistance=1k package=THT]
  DS18_Pull_Up = Resistor [tolerance=±5% power=0.25W resistance=4.7k package=THT]
  J1 = Screw terminal - 2 pins [package=THT]
  Q1 = MOSFET-NCHANNEL [package=to220v]
  A1 = mini560 [part_number=Mini560 package=THT]
  power_Jack = Power Jack [package=power_jack_pth_lock]
  Solenoid_Jack = Power Jack [package=power_jack_pth_lock]
  R2 = Resistor [tolerance=±5% power=0.25W resistance=10k package=THT]
  M1 = DOIT Esp32 DevKit v1 (30 pins long, 11 pins width) [part_number=ESP32S-PIN30]
  C1 = Electrolytic Capacitor [capacitance=1µF voltage=35V package="100 mil [THT, electrolytic]"]
  D1 = Rectifier Diode [part_number=1N4001 package="300 mil [THT]"]
  R2_-_2_2k = Resistor [tolerance=±5% power=0.25W resistance=2.2k package=THT]
  Connect_OLED = JST-B4B-XH-A [part_number=B4B-XH-A package=THT]
  Connect_pressure = JST-B3B-XH-A [part_number=B3B-XH-A package=THT]
  connect_ds18b20 = JST-B3B-XH-A [part_number=B3B-XH-A package=THT]

nets:
  N1: R1.Pin_0, M1.D34, R2_-_2_2k.Pin_0
  N2: R1.Pin_1, Connect_pressure.pin3
  N3: DS18_Pull_Up.Pin_0, M1.D4, connect_ds18b20.pin3
  N4: DS18_Pull_Up.Pin_1, M1.3V3, Connect_OLED.pin2, connect_ds18b20.pin2
  N5: J1.pin1, Q1.S, A1.pin_3, A1.pin_4, A1.pin_6, A1.pin_7, power_Jack.GNDBREAK, R2.Pin_1, M1.GND, C1.-, R2_-_2_2k.Pin_1, Connect_OLED.pin1, Connect_pressure.pin1, connect_ds18b20.pin1
  N6: J1.pin2, A1.pin_8, A1.pin_9, M1.VIN, Connect_pressure.pin2
  N7: Q1.G, R2.Pin_0, M1.D27
  N8: Q1.D, Solenoid_Jack.GNDBREAK, D1.anode
  N9: A1.pin_1, A1.pin_2, power_Jack.PWR, Solenoid_Jack.PWR, C1.+, D1.cathode
  N10: M1.D21, Connect_OLED.pin4
  N11: M1.D22, Connect_OLED.pin3

custom parts:
  mini560: 5A DC-DC Mini 560 Step Down Stabilized Voltage Supply Module Output 3.3 5V 9V 12V Step-down Power Converter Board Module
  DOIT Esp32 DevKit v1 (30 pins long, 11 pins width): The DOIT Esp32 DevKit v1 is one of the development board created by DOIT to evaluate the ESP-WROOM-32 module. It is based on the ESP32 microcontroller that boasts Wifi, Bluetooth, Ethernet and Low Power support all in a single chip. (vanepp) made breadboard work, adjusted pin numbering and labels and reduced size of schematic and cleaned up pcb. This chip is 30pins long (2 x15) and 11 pins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
