# Fritzing sketch fermentpressure_v4_ferminator (saved by Fritzing 1.0.7)
stripboards: 2

parts:
  OLED_I2C1 = OLED 128x64 I2C Monochrome Display  # not connected
  DS18_Pull_Up = Resistor [tolerance=±5% power=0.25W resistance=4.7k package=THT]
  J1 = Screw terminal - 2 pins [package=THT]
  Q1 = MOSFET-NCHANNEL [package=to220v]
  A1 = mini560 [part_number=Mini560 package=THT]
  power_Jack = Power Jack [package=power_jack_pth_lock]
  Solenoid_Jack = Power Jack [package=power_jack_pth_lock]
  R2_-_10k = Resistor [tolerance=±5% power=0.25W resistance=10k package=THT]
  C1 = Electrolytic Capacitor [capacitance=1µF voltage=35V package="100 mil [THT, electrolytic]"]
  D1 = Rectifier Diode [part_number=1N4001 package="300 mil [THT]"]
  Connect_OLED = JST-B4B-XH-A [part_number=B4B-XH-A package=THT]
  connect_ds18b20 = JST-B3B-XH-A [part_number=B3B-XH-A package=THT]
  A2 = ESP32-S3 supermini
  converter_in1 = female pin header, 4 pins [form="♀ (female)"]
  converter_in2 = female pin header, 4 pins [form="♀ (female)"]
  converter_in3 = female pin header, 4 pins [form="♀ (female)"]
  Connect_buttons = JST-B4B-XH-A [part_number=B4B-XH-A package=THT]
  connect_oled_ferminator = JST-B3B-XH-A [part_number=B3B-XH-A package=THT]

nets:
  N1: DS18_Pull_Up.Pin_0, connect_ds18b20.pin3, A2.Pin_6
  3.3V: DS18_Pull_Up.Pin_1, Connect_OLED.pin2, connect_ds18b20.pin2, A2.Pin_38, converter_in1.pin2
  GND: J1.pin1, Q1.S, A1.pin_3, A1.pin_4, A1.pin_6, A1.pin_7, power_Jack.GNDBREAK, R2_-_10k.Pin_1, C1.-, Connect_OLED.pin1, connect_ds18b20.pin1, A2.Pin_39, converter_in1.pin1, connect_oled_ferminator.pin1
  5V: J1.pin2, A1.pin_9, A2.Pin_40
  N2: Q1.G, R2_-_10k.Pin_0, A2.Pin_10
  N3: Q1.D, Solenoid_Jack.GNDBREAK, D1.anode
  N4: A1.pin_1, A1.pin_2, power_Jack.PWR, Solenoid_Jack.PWR, C1.+, D1.cathode
  N5: Connect_OLED.pin3, A2.Pin_8, converter_in1.pin3
  N6: Connect_OLED.pin4, A2.Pin_9, converter_in1.pin4
  N7: A2.Pin_32, connect_oled_ferminator.pin3
  N8: A2.Pin_33, connect_oled_ferminator.pin2
  N9: A2.Pin_34, Connect_buttons.pin4
  N10: A2.Pin_35, Connect_buttons.pin3
  N11: A2.Pin_36, Connect_buttons.pin2
  N12: A2.Pin_37, Connect_buttons.pin1
  N13: converter_in2.pin1, converter_in3.pin2
  N14: converter_in2.pin2, converter_in3.pin1
  N15: converter_in2.pin3, converter_in3.pin3
  N16: converter_in2.pin4, converter_in3.pin4

custom parts:
  mini560: 5A DC-DC Mini 560 Step Down Stabilized Voltage Supply Module Output 3.3 5V 9V 12V Step-down Power Converter Board Module
  ESP32-S3 supermini: Esp32-S3 Development board ESP32 SuperMini development board ESP32 Development board WiFi Bluetooth.
