# Fritzing sketch oled&sensor block (saved by Fritzing 1.0.7)
stripboards: 1

parts:
  oled = female pin header, 4 pins [form="♀ (female)"]
  i2c = male pin header, 4 pins [form="♂ (male)"]
  converter_in = female pin header, 4 pins [form="♀ (female)"]
  converter_out_5 = female pin header, 4 pins [form="♀ (female)"]
  esp_input = JST XH 3A Male [chip_label=? package=THT]
  sensor_esp_mode = JST XH 3A Male [chip_label=? package=THT]
  sensor_ads_mode = JST XH 3A Male [chip_label=? package=THT]  # not connected
  ads = female pin header, 10 pins [form="♀ (female)"]

nets:
  GND: oled.pin1, i2c.pin1, converter_in.pin1
  VCC: oled.pin2, i2c.pin2, converter_in.pin2
  SCL: oled.pin3, i2c.pin3, converter_in.pin3
  SDA: oled.pin4, i2c.pin4, converter_in.pin4
  GND5: converter_out_5.pin1, ads.pin2, ads.pin5
  VDD5: converter_out_5.pin2, ads.pin1
  N1: converter_out_5.pin3, ads.pin3
  N2: converter_out_5.pin4, ads.pin4
  N3: esp_input.pin1, sensor_esp_mode.pin1
  N4: esp_input.pin2, sensor_esp_mode.pin2
  N5: esp_input.pin3, sensor_esp_mode.pin3

notes:
  +5V
  GND

custom parts:
  JST XH 3A Male: 2.54 Mm JST "XH" connector
